// Logisim project circuit1a.circ as structural Verilog: 1 circuit, main circuit main
module main (
  input  A,
  input  B,
  input  C,
  output result
);

  wire and_1_out, and_2_out, and_3_out, and_4_out, not_1_out, not_2_out, not_3_out, not_4_out, or_1_out;

  not not_1 (not_1_out, A);
  not not_2 (not_2_out, B);
  not not_3 (not_3_out, C);
  and and_1 (and_1_out, A, not_2_out);
  or or_1 (or_1_out, not_1_out, and_1_out);
  and and_2 (and_2_out, A, B);
  and and_3 (and_3_out, or_1_out, not_3_out);
  not not_4 (not_4_out, and_4_out);
  and and_4 (and_4_out, and_2_out, C);
  or or_2 (result, and_3_out, not_4_out);
endmodule
