// Logisim project my_adder.circ as structural Verilog: 2 circuits, main circuit fa_16bit
module fa_16bit (
  input  [15:0] A,
  input  [15:0] B,
  input  sub,
  output [15:0] result,
  output ovf
);

  wire FA0_cout, FA1_cout, FA2_cout, FA3_cout, FA4_cout, FA5_cout, FA6_cout, FA7_cout, FA8_cout, FA9_cout,
       FA10_cout, FA11_cout, FA12_cout, FA13_cout, T1, T5, T6, T7, T8, T9, T10, T11, T12, T13, T14, T15,
       Tout, Tout14, xor_2_out, xor_14_out, xor_15_out, xor_16_out;

  xor xor_1 (T15, B[15], sub);
  xor xor_2 (xor_2_out, B[4], sub);
  xor xor_3 (T5, B[5], sub);
  xor xor_4 (T7, B[7], sub);
  xor xor_5 (T8, B[8], sub);
  xor xor_6 (T9, B[9], sub);
  xor xor_7 (T10, B[10], sub);
  xor xor_8 (T11, B[11], sub);
  xor xor_9 (T12, B[12], sub);
  xor xor_10 (T13, B[13], sub);
  xor xor_11 (T14, B[14], sub);
  xor xor_12 (T6, B[6], sub);
  xor xor_13 (T1, B[1], sub);
  xor xor_14 (xor_14_out, B[2], sub);
  xor xor_15 (xor_15_out, B[3], sub);
  xor xor_16 (xor_16_out, B[0], sub);
  fa_1bit FA12 (.A(A[12]), .B(T12), .Cin(FA11_cout), .sum(result[12]), .Cout(FA12_cout));
  fa_1bit FA13 (.A(A[13]), .B(T13), .Cin(FA12_cout), .sum(result[13]), .Cout(FA13_cout));
  fa_1bit FA14 (.A(A[14]), .B(T14), .Cin(FA13_cout), .sum(result[14]), .Cout(Tout14));
  fa_1bit FA15 (.A(A[15]), .B(T15), .Cin(Tout14), .sum(result[15]), .Cout(Tout));
  fa_1bit FA8 (.A(A[8]), .B(T8), .Cin(FA7_cout), .sum(result[8]), .Cout(FA8_cout));
  fa_1bit FA9 (.A(A[9]), .B(T9), .Cin(FA8_cout), .sum(result[9]), .Cout(FA9_cout));
  fa_1bit FA10 (.A(A[10]), .B(T10), .Cin(FA9_cout), .sum(result[10]), .Cout(FA10_cout));
  fa_1bit FA11 (.A(A[11]), .B(T11), .Cin(FA10_cout), .sum(result[11]), .Cout(FA11_cout));
  fa_1bit FA4 (.A(A[4]), .B(xor_2_out), .Cin(FA3_cout), .sum(result[4]), .Cout(FA4_cout));
  fa_1bit FA5 (.A(A[5]), .B(T5), .Cin(FA4_cout), .sum(result[5]), .Cout(FA5_cout));
  fa_1bit FA6 (.A(A[6]), .B(T6), .Cin(FA5_cout), .sum(result[6]), .Cout(FA6_cout));
  fa_1bit FA7 (.A(A[7]), .B(T7), .Cin(FA6_cout), .sum(result[7]), .Cout(FA7_cout));
  fa_1bit FA1 (.A(A[1]), .B(T1), .Cin(FA0_cout), .sum(result[1]), .Cout(FA1_cout));
  fa_1bit FA2 (.A(A[2]), .B(xor_14_out), .Cin(FA1_cout), .sum(result[2]), .Cout(FA2_cout));
  fa_1bit FA3 (.A(A[3]), .B(xor_15_out), .Cin(FA2_cout), .sum(result[3]), .Cout(FA3_cout));
  fa_1bit FA0 (.A(A[0]), .B(xor_16_out), .Cin(sub), .sum(result[0]), .Cout(FA0_cout));
  xor xor_17 (ovf, Tout14, Tout);

  // Other names for the same wires on the sheet: S0 = result[0]; S1 = result[1]; S2 = result[2]; S3 = result[3];
  //   S4 = result[4]; S5 = result[5]; S6 = result[6]; S7 = result[7]; S8 = result[8]; S9 = result[9];
  //   S10 = result[10]; S11 = result[11]; S12 = result[12]; S13 = result[13]; S14 = result[14]; S15 = result[15];
  //   Tsub = sub
endmodule

module fa_1bit (
  input  A,
  input  B,
  input  Cin,
  output sum,
  output Cout
);

  wire and_1_out, and_2_out, and_3_out, or_1_out, xor_1_out;

  xor xor_1 (xor_1_out, A, B);
  xor xor_2 (sum, xor_1_out, Cin);
  and and_1 (and_1_out, A, B);
  and and_2 (and_2_out, A, Cin);
  and and_3 (and_3_out, B, Cin);
  or or_1 (or_1_out, and_1_out, and_2_out);
  or or_2 (Cout, or_1_out, and_3_out);
endmodule
