// Logisim project scorer.circ as structural Verilog: 1 circuit, main circuit main
module main (
  input  in_timeout,
  input  in_reset,
  input  in_fliparrow,
  output out_homeTO,
  output out_advantage,
  output out_arrow
);

  wire and_1_out, and_3_out, clock_1_out, not_1_out, not_2_out, or_1_out, S1_q, T0, T2, xor_1_out;

  Clock clock_1 (.out(clock_1_out));
  not not_1 (not_1_out, in_reset);
  D_Flip_Flop S1 (.D(T2), .clk(clock_1_out), .Q(S1_q));  // open: Qn, preset, reset
  D_Flip_Flop S0 (.D(T0), .clk(clock_1_out), .Q(out_arrow));  // open: Qn, preset, reset
  and and_1 (and_1_out, in_timeout, S1_q);
  not not_2 (not_2_out, and_1_out);
  xor xor_1 (xor_1_out, out_arrow, in_fliparrow);
  or or_1 (or_1_out, S1_q, in_timeout);
  and and_2 (T2, not_1_out, or_1_out);
  and and_3 (and_3_out, not_2_out, xor_1_out);
  and and_4 (T0, not_1_out, and_3_out);
  not not_3 (out_homeTO, S1_q);
  and and_5 (out_advantage, out_homeTO, out_arrow);
endmodule
