// Logisim project cpu.circ as structural Verilog: 10 circuits, main circuit main
module main (
  input  reset
);

  wire ALUSrc, clk, is_beq, is_bgez, is_input, is_j, is_jal, is_jr, is_output, jump, k0, k1, k2, k3, k4, k5,
       k6, keyboard_1_avail, memory_latch_1_oe_latched, memory_latch_1_we_latched, MemToReg, MemWrite, nclk,
       or_1_out, or_2_out, or_3_out, or_4_out, or_5_out, Rdst, RegWriteEnable, xor_1_out, xor_2_out,
       xor_3_out, xor_4_out, xor_5_out, xor_6_out, xor_7_out, xor_8_out, xor_9_out, xor_10_out, xor_11_out,
       xor_12_out, xor_13_out, xor_14_out, xor_15_out, xor_16_out, Zero;
  wire [2:0] multiplexer_1_out, rd, rs, rt, shamt, WR;
  wire [3:0] ALUop;
  wire [5:0] Imm6;
  wire [6:0] bit_extender_1_out;
  wire [7:7] kbd_value;
  wire [11:0] Addr12;
  wire [15:0] ALU_result, Imm16, instr, MemData, memory_latch_1_address_latched,
       memory_latch_1_data_in_latched, Mout, PC, PCNext, PCplus1, RF_A, RF_B, wd_after_input, wd_after_mem,
       WriteData;

  Clock clock_1 (.out(clk));
  // Probe on PCNext
  not not_1 (nclk, clk);
  // Probe on bit_extender_1_out
  // Probe on RF_B[7:0]
  Bit_Extender #(.in_width(16), .out_width(7)) bit_extender_1 (.in(RF_A), .out(bit_extender_1_out));
  TTY #(.rows(13), .cols(80)) tty_1 (.data(bit_extender_1_out), .clk(clk), .we(is_output), .clr(reset));
  // Probe on PC
  Reg16 reg16_1 (.clk(nclk), .reset(reset), .D(PCNext), .WE(1'b1), .out_5(PC));
  ROM #(.addrWidth(16), .dataWidth(16)) rom_1 (.addr(PC), .data(instr));
  Keyboard #(.trigger("falling")) keyboard_1 (
    .clk(nclk), .re(is_input), .clr(reset), .avail(keyboard_1_avail), .data({k6, k5, k4, k3, k2, k1, k0}));
  // Probe on instr
  not not_2 (kbd_value[7], keyboard_1_avail);
  // Probe on {{8{1'b0}}, kbd_value[7], k6, k5, k4, k3, k2, k1, k0}
  // Probe on rs
  InstrDecode instrdecode_1 (
    .instr(instr), .rs(rs), .rt(rt), .is_beq(is_beq), .is_bgez(is_bgez), .is_j(is_j), .rd(rd), .is_jr(is_jr),
    .is_jal(is_jal), .ALUop(ALUop), .Imm6(Imm6), .shamt(shamt), .RegWriteEnable(RegWriteEnable),
    .Addr12(Addr12), .ALUSrc(ALUSrc), .MemWrite(MemWrite), .MemToReg(MemToReg), .is_input(is_input),
    .Jump(jump), .is_output(is_output), .Rdst(Rdst));  // open: Branch
  // Probe on rt
  // Probe on rd
  Multiplexer #(.width(3), .enable("false")) multiplexer_1 (.in0(rt), .in1(rd), .out(multiplexer_1_out), .sel(Rdst));
  // Probe on WR
  // Probe on WriteData
  Multiplexer #(.width(3), .enable("false")) multiplexer_2 (
    .in0(multiplexer_1_out), .in1(3'b111), .out(WR), .sel(jump));
  // Probe on RF_B
  RegisterFile registerfile_1 (
    .clk(clk), .reset(reset), .RegWriteEnable(RegWriteEnable), .ReadReg1(rs), .ReadReg2(rt), .WriteReg(WR),
    .WriteData(WriteData), .ReadData2(RF_B), .ReadData1(RF_A));
  // Probe on RF_A
  // Probe on PCplus1
  NextPC nextpc_1 (
    .PC(PC), .Imm16(Imm16), .Addr12(Addr12), .RR1Val(RF_A), .Zero(Zero), .is_beq(is_beq), .is_bgez(is_bgez),
    .is_j(is_j), .is_jr(is_jr), .is_jal(is_jal), .PCplus1(PCplus1), .NextPC(PCNext));
  // Probe on PCNext
  xor xor_1 (xor_1_out, RF_A[0], RF_B[0]);
  xor xor_2 (xor_2_out, RF_A[1], RF_B[1]);
  xor xor_3 (xor_3_out, RF_A[2], RF_B[2]);
  xor xor_4 (xor_4_out, RF_A[3], RF_B[3]);
  xor xor_5 (xor_5_out, RF_A[4], RF_B[4]);
  xor xor_6 (xor_6_out, RF_A[5], RF_B[5]);
  xor xor_7 (xor_7_out, RF_A[6], RF_B[6]);
  xor xor_8 (xor_8_out, RF_A[7], RF_B[7]);
  xor xor_9 (xor_9_out, RF_A[8], RF_B[8]);
  xor xor_10 (xor_10_out, RF_A[9], RF_B[9]);
  xor xor_11 (xor_11_out, RF_A[10], RF_B[10]);
  xor xor_12 (xor_12_out, RF_A[11], RF_B[11]);
  xor xor_13 (xor_13_out, RF_A[12], RF_B[12]);
  xor xor_14 (xor_14_out, RF_A[13], RF_B[13]);
  xor xor_15 (xor_15_out, RF_A[14], RF_B[14]);
  xor xor_16 (xor_16_out, RF_A[15], RF_B[15]);
  // Probe on Mout
  or or_1 (or_1_out, xor_1_out, xor_2_out, xor_3_out, xor_4_out);
  or or_2 (or_2_out, xor_5_out, xor_6_out, xor_7_out, xor_8_out);
  or or_3 (or_3_out, xor_9_out, xor_10_out, xor_11_out, xor_12_out);
  or or_4 (or_4_out, xor_13_out, xor_14_out, xor_15_out, xor_16_out);
  // Probe on RF_A
  or or_5 (or_5_out, or_1_out, or_2_out, or_3_out, or_4_out);
  assign Imm16 = {{10{Imm6[5]}}, Imm6};  // Bit_Extender bit_extender_2
  // Probe on Mout
  Multiplexer #(.width(16), .enable("false")) multiplexer_3 (.in0(RF_B), .in1(Imm16), .out(Mout), .sel(ALUSrc));
  not not_3 (Zero, or_5_out);
  // Probe on ALU_result
  ALU alu_1 (.A(RF_A), .B(Mout), .ALUop(ALUop), .shamt(shamt), .Result(ALU_result));
  // Probe on Imm16
  // Probe on wd_after_input
  Multiplexer #(.width(16), .enable("false")) multiplexer_4 (
    .in0(ALU_result), .in1(MemData), .out(wd_after_input), .sel(MemToReg));
  // Probe on wd_after_mem
  Multiplexer #(.width(16), .enable("false")) multiplexer_5 (
    .in0(wd_after_input), .in1({{8{1'b0}}, kbd_value[7], k6, k5, k4, k3, k2, k1, k0}), .out(wd_after_mem),
    .sel(is_input));
  memory_latch memory_latch_1 (
    .address(ALU_result), .WE(MemWrite), .clk(nclk), .data_in(RF_B),
    .address_latched(memory_latch_1_address_latched), .WE_latched(memory_latch_1_we_latched),
    .OE_latched(memory_latch_1_oe_latched), .data_in_latched(memory_latch_1_data_in_latched));
  Multiplexer #(.width(16), .enable("false")) multiplexer_6 (
    .in0(wd_after_mem), .in1(PCplus1), .out(WriteData), .sel(jump));
  RAM #(.addrWidth(16), .dataWidth(16), .trigger("high"), .databus("bibus")) ram_1 (
    .addr(memory_latch_1_address_latched), .we(memory_latch_1_we_latched), .oe(memory_latch_1_oe_latched),
    .din(memory_latch_1_data_in_latched), .dout(MemData));
  // Probe on WriteData
  // Probe on MemData

  // Other names for the same wires on the sheet: kbd_value[6:0] = {k6, k5, k4, k3, k2, k1, k0}; na = kbd_value[7];
  //   RFA0 = RF_A[0]; RFA1 = RF_A[1]; RFA2 = RF_A[2]; RFA3 = RF_A[3]; RFA4 = RF_A[4]; RFA5 = RF_A[5]; RFA6 = RF_A[6];
  //   RFA7 = RF_A[7]; RFA8 = RF_A[8]; RFA9 = RF_A[9]; RFA10 = RF_A[10]; RFA11 = RF_A[11]; RFA12 = RF_A[12];
  //   RFA13 = RF_A[13]; RFA14 = RF_A[14]; RFA15 = RF_A[15]; RFB8 = RF_B[8]; RFB9 = RF_B[9]; RFB10 = RF_B[10];
  //   RFB11 = RF_B[11]; RFB12 = RF_B[12]; RFB13 = RF_B[13]; RFB14 = RF_B[14]; RFB15 = RF_B[15]; RFB0 = RF_B[0];
  //   ttydata[7:0] = RF_B[7:0]; RFB1 = RF_B[1]; RFB2 = RF_B[2]; RFB3 = RF_B[3]; RFB4 = RF_B[4]; RFB5 = RF_B[5];
  //   RFB6 = RF_B[6]; RFB7 = RF_B[7]

  // Notes on the sheet:
  //   contents of rom_1 (hex, n*v repeats v):
  //   4a e008 2a0 f400 e008 2a0 f400 e008 2a0 f400 903f
endmodule

module RegisterFile (
  input  clk,
  input  reset,
  input  RegWriteEnable,
  input  [2:0] ReadReg1,
  input  [2:0] ReadReg2,
  input  [2:0] WriteReg,
  input  [15:0] WriteData,
  output [15:0] ReadData2,
  output [15:0] ReadData1
);

  wire A0, A1, A2, A3, A4, A5, A6, A7, D0, D1, D2, D3, D4, D5, D6, D7, E0, E1, E2, E3, E4, E5, E6, E7, EE0,
       EE1, EE2, EE3, EE4, EE5, EE6, EE7;
  wire [15:0] reg0_out_5, reg1_out_5, reg2_out_5, reg3_out_5, reg4_out_5, reg5_out_5, reg6_out_5, reg7_out_5;

  // Probe on WriteData
  Decoder #(.select(3)) decoder_1 (
    .out0(E0), .out1(E1), .out2(E2), .out3(E3), .out4(E4), .out5(E5), .out6(E6), .out7(E7), .sel(ReadReg1),
    .en(1'b1));
  Decoder #(.select(3)) decoder_2 (
    .out0(D0), .out1(D1), .out2(D2), .out3(D3), .out4(D4), .out5(D5), .out6(D6), .out7(D7), .sel(WriteReg),
    .en(RegWriteEnable));
  Decoder #(.select(3)) decoder_3 (
    .out0(EE0), .out1(EE1), .out2(EE2), .out3(EE3), .out4(EE4), .out5(EE5), .out6(EE6), .out7(EE7),
    .sel(ReadReg2), .en(1'b1));
  // Probe on reg0_out_5
  Reg16 reg0 (.clk(clk), .reset(reset), .D(WriteData), .WE(1'b0), .out_5(reg0_out_5));
  // Probe on reg1_out_5
  Reg16 reg1 (.clk(clk), .reset(reset), .D(WriteData), .WE(A1), .out_5(reg1_out_5));
  // Probe on reg2_out_5
  Reg16 reg2 (.clk(clk), .reset(reset), .D(WriteData), .WE(A2), .out_5(reg2_out_5));
  // Probe on reg3_out_5
  Reg16 reg3 (.clk(clk), .reset(reset), .D(WriteData), .WE(A3), .out_5(reg3_out_5));
  // Probe on reg4_out_5
  Reg16 reg4 (.clk(clk), .reset(reset), .D(WriteData), .WE(A4), .out_5(reg4_out_5));
  // Probe on reg5_out_5
  Reg16 reg5 (.clk(clk), .reset(reset), .D(WriteData), .WE(A5), .out_5(reg5_out_5));
  // Probe on reg6_out_5
  Reg16 reg6 (.clk(clk), .reset(reset), .D(WriteData), .WE(A6), .out_5(reg6_out_5));
  // Probe on reg7_out_5
  Reg16 reg7 (.clk(clk), .reset(reset), .D(WriteData), .WE(A7), .out_5(reg7_out_5));
  assign ReadData1 = E0 ? reg0_out_5 : 16'bz;  // Controlled_Buffer controlled_buffer_1
  assign ReadData2 = EE0 ? reg0_out_5 : 16'bz;  // Controlled_Buffer controlled_buffer_2
  assign ReadData1 = E1 ? reg1_out_5 : 16'bz;  // Controlled_Buffer controlled_buffer_3
  assign ReadData2 = EE1 ? reg1_out_5 : 16'bz;  // Controlled_Buffer controlled_buffer_4
  assign ReadData1 = E2 ? reg2_out_5 : 16'bz;  // Controlled_Buffer controlled_buffer_5
  assign ReadData2 = EE2 ? reg2_out_5 : 16'bz;  // Controlled_Buffer controlled_buffer_6
  assign ReadData1 = E3 ? reg3_out_5 : 16'bz;  // Controlled_Buffer controlled_buffer_7
  assign ReadData2 = EE3 ? reg3_out_5 : 16'bz;  // Controlled_Buffer controlled_buffer_8
  assign ReadData1 = E4 ? reg4_out_5 : 16'bz;  // Controlled_Buffer controlled_buffer_9
  assign ReadData2 = EE4 ? reg4_out_5 : 16'bz;  // Controlled_Buffer controlled_buffer_10
  assign ReadData1 = E5 ? reg5_out_5 : 16'bz;  // Controlled_Buffer controlled_buffer_11
  assign ReadData2 = EE5 ? reg5_out_5 : 16'bz;  // Controlled_Buffer controlled_buffer_12
  assign ReadData1 = E6 ? reg6_out_5 : 16'bz;  // Controlled_Buffer controlled_buffer_13
  assign ReadData2 = EE6 ? reg6_out_5 : 16'bz;  // Controlled_Buffer controlled_buffer_14
  assign ReadData1 = E7 ? reg7_out_5 : 16'bz;  // Controlled_Buffer controlled_buffer_15
  assign ReadData2 = EE7 ? reg7_out_5 : 16'bz;  // Controlled_Buffer controlled_buffer_16
  and and_1 (A0, D0, RegWriteEnable);
  and and_2 (A1, D1, RegWriteEnable);
  and and_3 (A2, D2, RegWriteEnable);
  and and_4 (A3, D3, RegWriteEnable);
  and and_5 (A4, D4, RegWriteEnable);
  and and_6 (A5, D5, RegWriteEnable);
  and and_7 (A6, D6, RegWriteEnable);
  and and_8 (A7, D7, RegWriteEnable);

  // Other names for the same wires on the sheet: clock = clk; RR1[2:0] = ReadReg1; RR2[2:0] = ReadReg2;
  //   RWE = RegWriteEnable; WD[15:0] = WriteData; WReg[2:0] = WriteReg
endmodule

module ALU (
  input  [15:0] A,
  input  [15:0] B,
  input  [3:0] ALUop,
  input  [2:0] shamt,
  output [15:0] Result
);

  wire [3:0] multiplexer_4_out;
  wire [11:0] multiplexer_4_out_2;
  wire [15:0] ADD_result, AND_result, multiplexer_1_out, multiplexer_2_out, Not_B, NOT_result, SLL_result,
       SRL_result, SUB_result;
  wire [15:4] multiplexer_3_out_2;
  wire [15:12] multiplexer_3_out;

  assign Not_B = ~B;  // NOT_Gate not_1, 16 bits wide
  // Probe on ADD_result
  fa_16bit fa_16bit_1 (.A(A), .B(B), .sub(1'b0), .result(ADD_result));  // open: ovf
  fa_16bit fa_16bit_2 (.A(A), .B(B), .sub(1'b1), .result(SUB_result));  // open: ovf
  assign AND_result = A & B;  // AND_Gate and_1, 16 bits wide
  // Probe on NOT_result
  assign NOT_result = ~A;  // NOT_Gate not_2, 16 bits wide
  // Probe on SUB_result
  // Probe on AND_result
  Multiplexer #(.width(16), .enable("false")) multiplexer_1 (
    .in0(A), .in1({1'b0, A[15:1]}), .out(multiplexer_1_out), .sel(shamt[0]));
  Multiplexer #(.width(16), .enable("false")) multiplexer_2 (
    .in0(A), .in1({A[14:0], 1'b0}), .out(multiplexer_2_out), .sel(shamt[0]));
  Multiplexer #(.width(16), .enable("false")) multiplexer_3 (
    .in0(multiplexer_2_out), .in1({multiplexer_2_out[13:0], 2'b00}),
    .out({multiplexer_3_out, multiplexer_3_out_2}), .sel(shamt[1]));
  Multiplexer #(.width(16), .enable("false")) multiplexer_4 (
    .in0(multiplexer_1_out), .in1({2'b00, multiplexer_1_out[15:2]}),
    .out({multiplexer_4_out_2, multiplexer_4_out}), .sel(shamt[1]));
  // Probe on Result
  Multiplexer #(.select(4), .width(16), .enable("false")) multiplexer_5 (
    .in0(ADD_result), .in1(SUB_result), .in2(ADD_result), .in3(NOT_result), .in4(AND_result),
    .in5(SLL_result), .in6(SRL_result), .in7(ADD_result), .in8(ADD_result), .in9(ADD_result),
    .in10(ADD_result), .in11({16{1'b0}}), .in12({16{1'b0}}), .in13({16{1'b0}}), .in14({16{1'b0}}),
    .in15({16{1'b0}}), .out(Result), .sel(ALUop));
  Multiplexer #(.width(16), .enable("false")) multiplexer_6 (
    .in0({multiplexer_3_out, multiplexer_3_out_2}), .in1({multiplexer_3_out_2, 4'b0000}), .out(SLL_result),
    .sel(shamt[2]));
  Multiplexer #(.width(16), .enable("false")) multiplexer_7 (
    .in0({multiplexer_4_out_2, multiplexer_4_out}), .in1({4'b0000, multiplexer_4_out_2}), .out(SRL_result),
    .sel(shamt[2]));
  // Probe on SLL_result
  // Probe on SRL_result

  // Other names for the same wires on the sheet: s0 = shamt[0]; s1 = shamt[1]; s2 = shamt[2]
endmodule

module InstrDecode (
  input  [15:0] instr,
  output [2:0] rs,
  output [2:0] rt,
  output is_beq,
  output is_bgez,
  output is_j,
  output [2:0] rd,
  output is_jr,
  output is_jal,
  output [3:0] ALUop,
  output [5:0] Imm6,
  output [2:0] shamt,
  output RegWriteEnable,
  output [11:0] Addr12,
  output ALUSrc,
  output MemWrite,
  output MemToReg,
  output Branch,
  output is_input,
  output Jump,
  output is_output,
  output Rdst
);

  wire is_add, is_addi, is_and, is_lw, is_not, is_sll, is_srl, is_sub, not_1_out, not_2_out, not_3_out,
       not_4_out, not_5_out, t1, t2;

  not not_1 (not_1_out, instr[14]);
  not not_2 (not_2_out, instr[13]);
  not not_3 (not_3_out, instr[12]);
  not not_4 (not_4_out, instr[14]);
  not not_5 (not_5_out, instr[13]);
  and and_1 (t1, instr[15], not_1_out);
  and and_2 (t2, t1, not_2_out);
  // AND_Gate and_3 has open pins: in0=t2, in1=not_3_out, out=open
  and and_4 (t1, instr[15], not_4_out);
  and and_5 (t2, t1, not_5_out);
  // AND_Gate and_6 has open pins: in0=t2, in1=instr[12], out=open
  Decoder #(.select(4)) decoder_1 (
    .out0(is_addi), .out1(is_sub), .out2(is_add), .out3(is_not), .out4(is_and), .out5(is_sll), .out6(is_srl),
    .out7(is_lw), .out8(MemWrite), .out9(is_bgez), .out10(is_beq), .out11(is_j), .out12(is_jr),
    .out13(is_jal), .out14(is_input), .out15(is_output), .sel(instr[15:12]), .en(1'b1));
  or or_1 (RegWriteEnable, is_addi, is_sub, is_and, is_not, is_sll, is_srl, is_add, is_lw, is_input, is_jal);
  or or_2 (ALUSrc, is_addi, is_lw, MemWrite);
  or or_3 (MemToReg, is_lw, is_input);
  or or_4 (Branch, is_beq, is_bgez);
  or or_5 (Jump, is_j, is_jr, is_jal);
  or or_6 (Rdst, is_add, is_sub, is_srl, is_not, is_and, is_sll, is_input);

  assign Addr12 = instr[11:0];
  assign ALUop = instr[15:12];
  assign Imm6 = instr[5:0];
  assign rd = instr[5:3];
  assign rs = instr[11:9];
  assign rt = instr[8:6];
  assign shamt = instr[2:0];

  // Other names for the same wires on the sheet: B12 = instr[12]; B13 = instr[13]; B14 = instr[14]; B15 = instr[15];
  //   B00 = instr[0]; B01 = instr[1]; B02 = instr[2]; B03 = instr[3]; B04 = instr[4]; B05 = instr[5]; B06 = instr[6];
  //   B07 = instr[7]; B08 = instr[8]; B09 = instr[9]; B10 = instr[10]; B11 = instr[11]; is_sw = MemWrite
endmodule

module NextPC (
  input  [15:0] PC,
  input  [15:0] Imm16,
  input  [11:0] Addr12,
  input  [15:0] RR1Val,
  input  Zero,
  input  is_beq,
  input  is_bgez,
  input  is_j,
  input  is_jr,
  input  is_jal,
  output [15:0] PCplus1,
  output [15:0] NextPC
);

  wire AnyJump, NotSign, TakeBEQ, TakeBGEZ, TakeBranch;
  wire [15:0] AfterBranch, JumpTarget, PCbranch;

  fa_16bit fa_16bit_1 (.A(PC), .B(16'h1), .sub(1'b0), .result(PCplus1));  // open: ovf
  fa_16bit fa_16bit_2 (.A(PCplus1), .B(Imm16), .sub(1'b0), .result(PCbranch));  // open: ovf
  Multiplexer #(.width(16), .enable("false")) multiplexer_1 (
    .in0(PCplus1), .in1(PCbranch), .out(AfterBranch), .sel(TakeBranch));
  Multiplexer #(.width(16), .enable("false")) multiplexer_2 (
    .in0({PCplus1[15:12], Addr12}), .in1(RR1Val), .out(JumpTarget), .sel(is_jr));
  or or_1 (AnyJump, is_jr, is_j, is_jal);
  Multiplexer #(.width(16), .enable("false")) multiplexer_3 (
    .in0(AfterBranch), .in1(JumpTarget), .out(NextPC), .sel(AnyJump));
  not not_1 (NotSign, RR1Val[15]);
  and and_1 (TakeBEQ, is_beq, Zero);
  or or_2 (TakeBranch, TakeBEQ, TakeBGEZ);
  and and_2 (TakeBGEZ, is_bgez, NotSign);

  // Other names for the same wires on the sheet: PCjr[15:0] = RR1Val; SignRS = RR1Val[15]; A0 = Addr12[0];
  //   PCjump[15:0] = {PCplus1[15:12], Addr12}; A1 = Addr12[1]; PCplus1_int[15:0] = PCplus1
endmodule

module SignExtend6to16 (
  input  [5:0] imm6,
  output [15:0] imm16
);


  assign imm16 = {{11{imm6[5]}}, imm6[4:0]};

  // Other names for the same wires on the sheet: b0 = imm6[0]; b1 = imm6[1]; b2 = imm6[2]; b3 = imm6[3]; b4 = imm6[4];
  //   sb = imm6[5]
endmodule

module Reg16 (
  input  clk,
  input  reset,
  input  [15:0] D,
  input  WE,
  output [15:0] out_5
);

  wire m0, m1, m2, m3, m4, m5, m6, m7, m8, m9, m10, m11, m12, m13, m14, m15;

  Multiplexer #(.width(16), .enable("false")) multiplexer_1 (
    .in0(out_5), .in1(D), .out({m15, m14, m13, m12, m11, m10, m9, m8, m7, m6, m5, m4, m3, m2, m1, m0}),
    .sel(WE));
  D_Flip_Flop d_ff_1 (.D(m0), .clk(clk), .Q(out_5[0]), .reset(reset));  // open: Qn, preset
  D_Flip_Flop d_ff_2 (.D(m1), .clk(clk), .Q(out_5[1]), .reset(reset));  // open: Qn, preset
  D_Flip_Flop d_ff_3 (.D(m2), .clk(clk), .Q(out_5[2]), .reset(reset));  // open: Qn, preset
  D_Flip_Flop d_ff_4 (.D(m3), .clk(clk), .Q(out_5[3]), .reset(reset));  // open: Qn, preset
  D_Flip_Flop d_ff_5 (.D(m4), .clk(clk), .Q(out_5[4]), .reset(reset));  // open: Qn, preset
  D_Flip_Flop d_ff_6 (.D(m5), .clk(clk), .Q(out_5[5]), .reset(reset));  // open: Qn, preset
  D_Flip_Flop d_ff_7 (.D(m6), .clk(clk), .Q(out_5[6]), .reset(reset));  // open: Qn, preset
  D_Flip_Flop d_ff_8 (.D(m7), .clk(clk), .Q(out_5[7]), .reset(reset));  // open: Qn, preset
  D_Flip_Flop d_ff_9 (.D(m8), .clk(clk), .Q(out_5[8]), .reset(reset));  // open: Qn, preset
  D_Flip_Flop d_ff_10 (.D(m9), .clk(clk), .Q(out_5[9]), .reset(reset));  // open: Qn, preset
  D_Flip_Flop d_ff_11 (.D(m10), .clk(clk), .Q(out_5[10]), .reset(reset));  // open: Qn, preset
  D_Flip_Flop d_ff_12 (.D(m11), .clk(clk), .Q(out_5[11]), .reset(reset));  // open: Qn, preset
  D_Flip_Flop d_ff_13 (.D(m12), .clk(clk), .Q(out_5[12]), .reset(reset));  // open: Qn, preset
  D_Flip_Flop d_ff_14 (.D(m13), .clk(clk), .Q(out_5[13]), .reset(reset));  // open: Qn, preset
  D_Flip_Flop d_ff_15 (.D(m14), .clk(clk), .Q(out_5[14]), .reset(reset));  // open: Qn, preset
  D_Flip_Flop d_ff_16 (.D(m15), .clk(clk), .Q(out_5[15]), .reset(reset));  // open: Qn, preset

  // Other names for the same wires on the sheet: Q0 = out_5[0]; Qbus[15:0] = out_5; Q1 = out_5[1]; Q2 = out_5[2];
  //   Q3 = out_5[3]; Q4 = out_5[4]; Q5 = out_5[5]; Q6 = out_5[6]; Q7 = out_5[7]; Q8 = out_5[8]; Q9 = out_5[9];
  //   Q10 = out_5[10]; Q11 = out_5[11]; Q12 = out_5[12]; Q13 = out_5[13]; Q14 = out_5[14]; Q15 = out_5[15]
endmodule

module memory_latch (
  input  [15:0] address,
  input  WE,
  input  clk,
  input  [15:0] data_in,
  output [15:0] address_latched,
  output WE_latched,
  output OE_latched,
  output [15:0] data_in_latched
);

  wire DMwe_latch_q;
  wire [15:0] addr_latch_q;

  Register #(.width(16), .trigger("falling")) addr_latch (
    .D(address), .en(WE), .clk(clk), .Q(addr_latch_q));  // open: clr
  D_Flip_Flop #(.trigger("falling")) DMwe_latch (.D(WE), .clk(clk), .Q(DMwe_latch_q));  // open: Qn, preset, reset
  Register #(.width(16), .trigger("falling")) data_to_be_written (
    .D(data_in), .en(WE), .clk(clk), .Q(data_in_latched));  // open: clr
  Multiplexer #(.width(16), .enable("false")) multiplexer_1 (
    .in0(address), .in1(addr_latch_q), .out(address_latched), .sel(DMwe_latch_q));
  and and_1 (WE_latched, clk, DMwe_latch_q);
  not not_1 (OE_latched, WE_latched);
endmodule

module fa_16bit (
  input  [15:0] A,
  input  [15:0] B,
  input  sub,
  output [15:0] result,
  output ovf
);

  wire FA0_cout, FA1_cout, FA2_cout, FA3_cout, FA4_cout, FA5_cout, FA6_cout, FA7_cout, FA8_cout, FA9_cout,
       FA10_cout, FA11_cout, FA12_cout, FA13_cout, T1, T5, T6, T7, T8, T9, T10, T11, T12, T13, T14, T15,
       Tout, Tout14, xor_2_out, xor_14_out, xor_15_out, xor_16_out;

  xor xor_1 (T15, B[15], sub);
  xor xor_2 (xor_2_out, B[4], sub);
  xor xor_3 (T5, B[5], sub);
  xor xor_4 (T7, B[7], sub);
  xor xor_5 (T8, B[8], sub);
  xor xor_6 (T9, B[9], sub);
  xor xor_7 (T10, B[10], sub);
  xor xor_8 (T11, B[11], sub);
  xor xor_9 (T12, B[12], sub);
  xor xor_10 (T13, B[13], sub);
  xor xor_11 (T14, B[14], sub);
  xor xor_12 (T6, B[6], sub);
  xor xor_13 (T1, B[1], sub);
  xor xor_14 (xor_14_out, B[2], sub);
  xor xor_15 (xor_15_out, B[3], sub);
  xor xor_16 (xor_16_out, B[0], sub);
  fa_1bit FA12 (.A(A[12]), .B(T12), .Cin(FA11_cout), .sum(result[12]), .Cout(FA12_cout));
  fa_1bit FA13 (.A(A[13]), .B(T13), .Cin(FA12_cout), .sum(result[13]), .Cout(FA13_cout));
  fa_1bit FA14 (.A(A[14]), .B(T14), .Cin(FA13_cout), .sum(result[14]), .Cout(Tout14));
  fa_1bit FA15 (.A(A[15]), .B(T15), .Cin(Tout14), .sum(result[15]), .Cout(Tout));
  fa_1bit FA8 (.A(A[8]), .B(T8), .Cin(FA7_cout), .sum(result[8]), .Cout(FA8_cout));
  fa_1bit FA9 (.A(A[9]), .B(T9), .Cin(FA8_cout), .sum(result[9]), .Cout(FA9_cout));
  fa_1bit FA10 (.A(A[10]), .B(T10), .Cin(FA9_cout), .sum(result[10]), .Cout(FA10_cout));
  fa_1bit FA11 (.A(A[11]), .B(T11), .Cin(FA10_cout), .sum(result[11]), .Cout(FA11_cout));
  fa_1bit FA4 (.A(A[4]), .B(xor_2_out), .Cin(FA3_cout), .sum(result[4]), .Cout(FA4_cout));
  fa_1bit FA5 (.A(A[5]), .B(T5), .Cin(FA4_cout), .sum(result[5]), .Cout(FA5_cout));
  fa_1bit FA6 (.A(A[6]), .B(T6), .Cin(FA5_cout), .sum(result[6]), .Cout(FA6_cout));
  fa_1bit FA7 (.A(A[7]), .B(T7), .Cin(FA6_cout), .sum(result[7]), .Cout(FA7_cout));
  fa_1bit FA1 (.A(A[1]), .B(T1), .Cin(FA0_cout), .sum(result[1]), .Cout(FA1_cout));
  fa_1bit FA2 (.A(A[2]), .B(xor_14_out), .Cin(FA1_cout), .sum(result[2]), .Cout(FA2_cout));
  fa_1bit FA3 (.A(A[3]), .B(xor_15_out), .Cin(FA2_cout), .sum(result[3]), .Cout(FA3_cout));
  fa_1bit FA0 (.A(A[0]), .B(xor_16_out), .Cin(sub), .sum(result[0]), .Cout(FA0_cout));
  xor xor_17 (ovf, Tout14, Tout);

  // Other names for the same wires on the sheet: S0 = result[0]; S1 = result[1]; S2 = result[2]; S3 = result[3];
  //   S4 = result[4]; S5 = result[5]; S6 = result[6]; S7 = result[7]; S8 = result[8]; S9 = result[9];
  //   S10 = result[10]; S11 = result[11]; S12 = result[12]; S13 = result[13]; S14 = result[14]; S15 = result[15];
  //   Tsub = sub
endmodule

module fa_1bit (
  input  A,
  input  B,
  input  Cin,
  output sum,
  output Cout
);

  wire and_1_out, and_2_out, and_3_out, or_1_out, xor_1_out;

  xor xor_1 (xor_1_out, A, B);
  xor xor_2 (sum, xor_1_out, Cin);
  and and_1 (and_1_out, A, B);
  and and_2 (and_2_out, A, Cin);
  and and_3 (and_3_out, B, Cin);
  or or_1 (or_1_out, and_1_out, and_2_out);
  or or_2 (Cout, or_1_out, and_3_out);
endmodule
